# Fritzing sketch sploder (saved by Fritzing 0.9.1b)
breadboards: 1

parts:
  Arduino_3_3V = Arduino Pro Mini v13
  R1 = Resistor [tolerance=±5% resistance=10k package=THT]
  S1 = Pushbutton [package="[THT]"]
  LIPO_(1_cell_400mAh) = DC Power [voltage=3.7V]
  S2 = Toggle Switch [package=THT]
  R2 = Resistor [tolerance=±5% resistance=220 package=THT]
  R3 = Resistor [tolerance=±5% resistance=1k package=THT]
  Arming_LED = LED - 5mm [color="Red (633nm)" package="5 mm [THT]"]
  Firing_LED = LED - 5mm [color="Red (633nm)" package="5 mm [THT]"]

nets:
  GND: Arduino_3_3V.GND, R1.Pin_1, S2.L2, R2.Pin_1, R3.Pin_1
  N1: Arduino_3_3V.RAW, S1.Pin_3, S1.Pin_4, LIPO_(1_cell_400mAh).V-
  N2: Arduino_3_3V.D8, S2.COM
  N3: Arduino_3_3V.D5_PWM, Firing_LED.anode
  N4: Arduino_3_3V.D4, Arming_LED.anode
  N5: Arduino_3_3V.D2, R1.Pin_0, S1.Pin_1, S1.Pin_2
  N6: R2.Pin_0, Arming_LED.cathode
  N7: R3.Pin_0, Firing_LED.cathode

notes:
  Sploder
  A connected button for doing stuff.
